// Logisim project lutcomp.circ as structural Verilog: 10 circuits, main circuit main
// 10
module main (
  input  RESET
);

  wire and_1_out, clock_1_out, decoder_1_out0, decoder_1_out1, decoder_1_out2, decoder_1_out3,
       decoder_1_out4, decoder_1_out5, decoder_1_out6, decoder_1_out7, decoder_1_out8, decoder_1_out9,
       decoder_1_out10, decoder_1_out11, decoder_1_out12, decoder_1_out13, decoder_1_out14, decoder_1_out15,
       decoder_2_out0, decoder_2_out1, decoder_2_out2, decoder_2_out3, decoder_2_out4, decoder_2_out5,
       decoder_2_out6, decoder_2_out7, decoder_2_out8, decoder_2_out9, decoder_2_out10, decoder_2_out11,
       decoder_2_out15, key_ctrl_1_key_clk, key_ctrl_1_key_read_en, key_ctrl_1_rdy, keyboard_1_avail,
       not_1_out, not_2_out, not_3_out, not_4_out, not_5_out, not_6_out, not_7_out, not_8_out, not_9_out,
       not_10_out, not_20_out, not_21_out, not_22_out, not_23_out, not_24_out, undriven, undriven_2,
       undriven_3, undriven_5;
  wire [1:0] IRH_2_q_2;
  wire [2:0] IRH_2_q, IRH_2_q_3;
  wire [6:0] keyboard_1_data, undriven_4;
  wire [7:0] ACC_q, ADDR_q, ALU_LUT_data, IRH_q, PC1_io_2, RAM_data, ROM_data, uPC_io_2, uROM_data, xADDR0_q,
       xADDR1_q, xADDR2_q, xRAM_data;
  wire [15:8] PC0_io_2;

  not not_1 (not_1_out, RESET);
  not not_2 (not_2_out, clock_1_out);
  Clock clock_1 (.out(clock_1_out));
  not not_3 (not_3_out, not_5_out);
  _74LS593 uPC (
    .IO(uPC_io_2), .CCK(not_2_out), .nCCLR(and_1_out), .IO_2(uPC_io_2));  // open: nCLOAD, G, nG, CCKEN, nCCKEN, nRCKEN, RCK, nRCO
  and and_1 (and_1_out, not_1_out, ~decoder_2_out15);  // AND_Gate
  _74LS593 PC1 (
    .G(1'b0), .nG(undriven), .IO(PC1_io_2), .nCCKEN(1'b0), .CCK(undriven_2), .nCCLR(not_1_out),
    .nRCKEN(1'b0), .RCK(undriven_3), .IO_2(PC1_io_2));  // open: nCLOAD, CCKEN, nRCO
  _74LS593 PC0 (
    .G(1'b0), .nG(not_9_out), .IO(PC0_io_2), .nCCKEN(1'b0), .CCK(not_3_out), .nCCLR(not_1_out),
    .nRCKEN(1'b0), .RCK(decoder_2_out5), .IO_2(PC0_io_2));  // open: nCLOAD, CCKEN, nRCO
  // Probe on PC0_io_2
  _74HCT374 IRH (.D({IRH_2_q_3, IRH_2_q_2, IRH_2_q}), .CP(not_2_out), .nOE(1'b0), .Q(IRH_q));
  // Probe on {IRH_q, uPC_io_2}
  // Probe on ROM_data
  ROM #(.Select("high")) ROM (.addr(PC0_io_2), .data(ROM_data));
  ROM #(.addrWidth(16), .Select("high")) uROM (.addr({IRH_q, uPC_io_2}), .data(uROM_data));
  not not_4 (not_4_out, decoder_1_out0);
  not not_5 (not_5_out, decoder_1_out1);
  not not_6 (not_6_out, decoder_1_out2);
  not not_7 (not_7_out, decoder_1_out3);
  not not_8 (not_8_out, decoder_1_out4);
  not not_9 (not_9_out, decoder_1_out5);
  not not_10 (not_10_out, decoder_1_out6);
  // NOT_Gate not_11 has open pins: in=decoder_1_out7, out=open
  // NOT_Gate not_12 has open pins: in=decoder_1_out8, out=open
  // NOT_Gate not_13 has open pins: in=decoder_1_out9, out=open
  // NOT_Gate not_14 has open pins: in=decoder_1_out10, out=open
  // NOT_Gate not_15 has open pins: in=decoder_1_out11, out=open
  // NOT_Gate not_16 has open pins: in=decoder_1_out12, out=open
  // NOT_Gate not_17 has open pins: in=decoder_1_out13, out=open
  // NOT_Gate not_18 has open pins: in=decoder_1_out14, out=open
  // NOT_Gate not_19 has open pins: in=decoder_1_out15, out=open
  Decoder #(.select(4), .disabled(0), .enable("false")) decoder_1 (
    .out0(decoder_1_out0), .out1(decoder_1_out1), .out2(decoder_1_out2), .out3(decoder_1_out3),
    .out4(decoder_1_out4), .out5(decoder_1_out5), .out6(decoder_1_out6), .out7(decoder_1_out7),
    .out8(decoder_1_out8), .out9(decoder_1_out9), .out10(decoder_1_out10), .out11(decoder_1_out11),
    .out12(decoder_1_out12), .out13(decoder_1_out13), .out14(decoder_1_out14), .out15(decoder_1_out15),
    .sel(uROM_data[7:4]));
  Decoder #(.select(4), .disabled(0)) decoder_2 (
    .out0(decoder_2_out0), .out1(decoder_2_out1), .out2(decoder_2_out2), .out3(decoder_2_out3),
    .out4(decoder_2_out4), .out5(decoder_2_out5), .out6(decoder_2_out6), .out7(decoder_2_out7),
    .out8(decoder_2_out8), .out9(decoder_2_out9), .out10(decoder_2_out10), .out11(decoder_2_out11),
    .out15(decoder_2_out15), .sel(uROM_data[3:0]), .en(clock_1_out));  // open: out12, out13, out14
  _74HCT374 IRL (.D(ROM_data), .CP(decoder_2_out0), .nOE(not_4_out), .Q(PC0_io_2));
  _74HCT374 IRH_2 (.D(ROM_data), .CP(decoder_2_out1), .nOE(1'b0), .Q({IRH_2_q_3, IRH_2_q_2, IRH_2_q}));
  _74HCT374 ACC (.D(PC0_io_2), .CP(decoder_2_out6), .nOE(1'b0), .Q(ACC_q));
  not not_20 (not_20_out, not_7_out);
  // Probe on ACC_q
  // Probe on {IRH_2_q_3, IRH_2_q_2, IRH_2_q}
  _74HCT299 TMP (
    .IO(PC0_io_2), .S0(not_20_out), .S1(not_20_out), .CP(decoder_2_out3), .nOE1(not_7_out), .nOE2(not_7_out),
    .IO_2(PC0_io_2));  // open: nMR
  _74HCT374 xADDR0 (.D(PC0_io_2), .CP(decoder_2_out8), .nOE(1'b0), .Q(xADDR0_q));
  _74HCT374 xADDR1 (.D(PC0_io_2), .CP(decoder_2_out9), .nOE(1'b0), .Q(xADDR1_q));
  _74HCT374 xADDR2 (.D(PC0_io_2), .CP(decoder_2_out10), .nOE(1'b0), .Q(xADDR2_q));
  not not_21 (not_21_out, decoder_2_out11);
  RAM #(.addrWidth(24), .bus("asynch"), .Select("high")) xRAM (
    .addr({xADDR2_q, xADDR1_q, xADDR0_q}), .data(xRAM_data), .ld(not_21_out));  // open: sel, clr
  _74HCT374 ADDR (.D(PC0_io_2), .CP(decoder_2_out7), .nOE(1'b0), .Q(ADDR_q));
  // Probe on PC0_io_2
  assign xRAM_data = not_10_out ? PC0_io_2 : 8'bz;  // Controlled_Buffer controlled_buffer_1
  assign PC0_io_2 = not_22_out ? xRAM_data : 8'bz;  // Controlled_Buffer controlled_buffer_2
  not not_22 (not_22_out, not_10_out);
  not not_23 (not_23_out, decoder_2_out4);
  RAM #(.bus("asynch"), .Select("high")) RAM (.addr(ADDR_q), .data(RAM_data), .ld(not_23_out));  // open: sel, clr
  assign PC0_io_2 = not_24_out ? RAM_data : 8'bz;  // Controlled_Buffer controlled_buffer_3
  not not_24 (not_24_out, not_8_out);
  ROM #(.addrWidth(19), .Select("high")) ALU_LUT (.addr({IRH_2_q_3, PC0_io_2, ACC_q}), .data(ALU_LUT_data));
  assign RAM_data = not_8_out ? PC0_io_2 : 8'bz;  // Controlled_Buffer controlled_buffer_4
  Keyboard keyboard_1 (
    .clk(key_ctrl_1_key_clk), .re(key_ctrl_1_key_read_en), .avail(keyboard_1_avail), .data(keyboard_1_data));  // open: clr
  _74HCT374 ALU (.D(ALU_LUT_data), .CP(decoder_2_out2), .nOE(not_6_out), .Q(PC0_io_2));
  TTY #(.trigger("falling")) tty_1 (.data(undriven_4));  // open: clk, we, clr
  key_ctrl key_ctrl_1 (
    .key_avail(keyboard_1_avail), .discard(undriven_5), .key_clk(key_ctrl_1_key_clk),
    .key_read_en(key_ctrl_1_key_read_en), .rdy(key_ctrl_1_rdy));

  // Notes on the sheet:
  //   contents of ROM (hex, n*v repeats v):
  //   10 1
  //   contents of uROM (hex, n*v repeats v):
  //   50 13 51 2 26 13 ff 249*0 50 63 51 7 42 26 63 ff
  //   contents of ALU_LUT (hex, n*v repeats v):
  //   256*0 256*1 256*2 256*3 256*4 256*5 256*6 256*7 256*8 256*9 256*a 256*b 256*c 256*d 256*e 256*f
  //   256*10 256*11 256*12 256*13 256*14 256*15 256*16 256*17 256*18 256*19 256*1a 256*1b 256*1c 256*1d
  //   256*1e 256*1f 256*20 256*21 256*22 256*23 256*24 256*25 256*26 256*27 256*28 256*29 256*2a 256*2b
  //   256*2c 256*2d 256*2e 256*2f 256*30 256*31 256*32 256*33 256*34 256*35 256*36 256*37 256*38 256*39
  //   256*3a 256*3b 256*3c 256*3d 256*3e 256*3f 256*40 256*41 256*42 256*43 256*44 256*45 256*46 256*47
  //   256*48 256*49 256*4a 256*4b 256*4c 256*4d 256*4e 256*4f 256*50 256*51 256*52 256*53 256*54 256*55
  //   256*56 256*57 256*58 256*59 256*5a 256*5b 256*5c 256*5d 256*5e 256*5f 256*60 256*61 256*62 256*63
  //   256*64 256*65 256*66 256*67 256*68 256*69 256*6a 256*6b 256*6c 256*6d 256*6e 256*6f 256*70 256*71
  //   256*72 256*73 256*74 256*75 256*76 256*77 256*78 256*79 256*7a 256*7b 256*7c 256*7d 256*7e 256*7f
  //   11008*0 ab
endmodule

module mmu (
  input  [7:0] data_in,
  input  [6:0] key_char,
  input  key_rdy,
  input  [23:0] addr,
  input  store,
  input  clk,
  output key_discard,
  output [6:0] ttydata,
  output ttyclk,
  output [7:0] data_out
);

  wire and_1_out, and_2_out, and_3_out, comparator_1_eq, comparator_1_gt, comparator_1_lt, not_1_out;
  wire [7:0] ram_1_data;

  assign data_out = store ? data_in : 8'bz;  // Controlled_Buffer controlled_buffer_1
  Comparator #(.width(24)) comparator_1 (
    .a(24'h1), .b(addr), .gt(comparator_1_gt), .eq(comparator_1_eq), .lt(comparator_1_lt));
  not not_1 (not_1_out, store);
  assign data_out = and_1_out ? {key_rdy, key_char} : 8'bz;  // Controlled_Buffer controlled_buffer_2
  and and_1 (and_1_out, comparator_1_gt, not_1_out);
  assign data_out = and_2_out ? 8'hcc : 8'bz;  // Controlled_Buffer controlled_buffer_3
  and and_2 (and_2_out, comparator_1_eq, not_1_out);
  RAM #(.addrWidth(24), .Select("high")) ram_1 (
    .addr(addr), .data(ram_1_data), .clk(clk), .ld(not_1_out));  // open: sel, clr
  assign ram_1_data = store ? data_out : 8'bz;  // Controlled_Buffer controlled_buffer_4
  assign data_out = and_3_out ? ram_1_data : 8'bz;  // Controlled_Buffer controlled_buffer_5
  and and_3 (and_3_out, comparator_1_lt, not_1_out);
  and and_4 (key_discard, data_out[7], store, clk, comparator_1_gt);
  and and_5 (ttyclk, comparator_1_eq, store, clk);

  assign ttydata = data_out[6:0];

  // Notes on the sheet:
  //   addr == 1
  //   addr > 1
  //   addr == 0
endmodule

module key_ctrl (
  input  key_avail,
  input  discard,
  output key_clk,
  output key_read_en,
  output rdy
);

  wire and_1_out, and_3_out, and_4_out, clock_1_out, d_ff_1_q, d_ff_2_q, decoder_1_out0, decoder_1_out1,
       decoder_1_out2, decoder_1_out3, decoder_1_out4;
  wire [2:0] counter_1_q;

  Clock clock_1 (.out(clock_1_out));
  Decoder #(.select(3), .disabled(0), .enable("false")) decoder_1 (
    .out0(decoder_1_out0), .out1(decoder_1_out1), .out2(decoder_1_out2), .out3(decoder_1_out3),
    .out4(decoder_1_out4), .sel(counter_1_q));  // open: out5, out6, out7
  Counter #(.width(3), .max('h4), .trigger("falling"), .behavior("old")) counter_1 (
    .Q(counter_1_q), .clk(clock_1_out));  // open: load, D, count, carry, clr, preset
  or or_1 (key_clk, decoder_1_out0, and_1_out);
  and and_1 (and_1_out, decoder_1_out2, d_ff_2_q);
  or or_2 (key_read_en, decoder_1_out1, decoder_1_out2);
  D_Flip_Flop d_ff_1 (.clk(and_1_out), .D(1'b1), .Q(d_ff_1_q), .reset(and_4_out));  // open: Qn, preset
  D_Flip_Flop d_ff_2 (.clk(discard), .D(1'b1), .Q(d_ff_2_q), .reset(and_4_out));  // open: Qn, preset
  and and_2 (rdy, key_avail, ~and_3_out);  // AND_Gate
  and and_3 (and_3_out, d_ff_1_q, decoder_1_out3);
  and and_4 (and_4_out, d_ff_1_q, decoder_1_out4);
endmodule

module regs (
  input  [3:0] D,
  input  [3:0] index,
  input  W,
  input  R,
  input  ADDR_CLK,
  output [3:0] QLO,
  output [3:0] QHI,
  output [3:0] Q,
  output [23:0] extADDR,
  output [7:0] ADDR
);

  wire and_1_out, and_2_out, not_1_out, sn74ls156_1__1y0, sn74ls156_1__1y1, sn74ls156_1__1y2,
       sn74ls156_1__1y3, sn74ls156_1__2y0, sn74ls156_1__2y1, sn74ls156_1__2y2, sn74ls156_1__2y3;

  SN74LS156 sn74ls156_1 (
    .n1G(W), ._1C(1'b1), .SEL({index[3], index[0]}), .n2G(R), ._2C(1'b1), ._1Y0(sn74ls156_1__1y0),
    ._1Y1(sn74ls156_1__1y1), ._1Y2(sn74ls156_1__1y2), ._1Y3(sn74ls156_1__1y3), ._2Y0(sn74ls156_1__2y0),
    ._2Y1(sn74ls156_1__2y1), ._2Y2(sn74ls156_1__2y2), ._2Y3(sn74ls156_1__2y3));
  and and_1 (and_1_out, sn74ls156_1__2y0, sn74ls156_1__2y1);
  and and_2 (and_2_out, sn74ls156_1__2y2, sn74ls156_1__2y3);
  SN74LS670 LO1 (.W(index[2:1]), .nGW(sn74ls156_1__1y0), .R(index[2:1]), .nGR(and_1_out), .IO(D), .IO_2(QLO));
  SN74LS670 HI1 (.W(index[2:1]), .nGW(sn74ls156_1__1y1), .R(index[2:1]), .nGR(and_1_out), .IO(D), .IO_2(QHI));
  SN74LS670 LO2 (.W(index[2:1]), .nGW(sn74ls156_1__1y2), .R(index[2:1]), .nGR(and_2_out), .IO(D), .IO_2(QLO));
  SN74LS670 HI2 (.W(index[2:1]), .nGW(sn74ls156_1__1y3), .R(index[2:1]), .nGR(and_2_out), .IO(D), .IO_2(QHI));
  Multiplexer #(.width(4)) multiplexer_1 (.in0(QLO), .in1(QHI), .out(D), .sel(index[0]), .en(not_1_out));
  not not_1 (not_1_out, R);
  _74HCT377 u_74hct377_1 (.D({QHI, QLO}), .nEN(sn74ls156_1__2y0), .CLK(ADDR_CLK), .Q(extADDR[7:0]));
  _74HCT377 u_74hct377_2 (.D({QHI, QLO}), .nEN(sn74ls156_1__2y1), .CLK(ADDR_CLK), .Q(extADDR[15:8]));
  _74HCT377 u_74hct377_3 (.D({QHI, QLO}), .nEN(sn74ls156_1__2y2), .CLK(ADDR_CLK), .Q(extADDR[23:16]));
  _74HCT377 u_74hct377_4 (.D({QHI, QLO}), .nEN(sn74ls156_1__2y3), .CLK(ADDR_CLK), .Q(ADDR));

  assign Q = D;

  // Notes on the sheet:
  //   W: pull=up
  //   R: pull=up
endmodule

module SN74LS670 (
  input  [1:0] W,
  input  nGW,
  input  [1:0] R,
  input  nGR,
  input  [3:0] IO,
  output [3:0] IO_2
);

  wire decoder_1_out0, decoder_1_out1, decoder_1_out2, decoder_1_out3, decoder_2_out0, decoder_2_out1,
       decoder_2_out2, decoder_2_out3, not_1_out;
  wire [3:0] register_1_q, register_2_q, register_3_q, register_4_q;

  not not_1 (not_1_out, nGR);
  Decoder #(.select(2), .disabled(0), .enable("false")) decoder_1 (
    .out0(decoder_1_out0), .out1(decoder_1_out1), .out2(decoder_1_out2), .out3(decoder_1_out3), .sel(W));
  Decoder #(.select(2), .disabled(0)) decoder_2 (
    .out0(decoder_2_out0), .out1(decoder_2_out1), .out2(decoder_2_out2), .out3(decoder_2_out3), .sel(R),
    .en(not_1_out));
  Register #(.width(4), .Select("low")) register_1 (
    .D(IO), .en(decoder_1_out0), .Q(register_1_q), .clk(nGW));  // open: clr
  Register #(.width(4), .Select("low")) register_2 (
    .D(IO), .en(decoder_1_out1), .Q(register_2_q), .clk(nGW));  // open: clr
  Register #(.width(4), .Select("low")) register_3 (
    .D(IO), .en(decoder_1_out2), .Q(register_3_q), .clk(nGW));  // open: clr
  Register #(.width(4), .Select("low")) register_4 (
    .D(IO), .en(decoder_1_out3), .Q(register_4_q), .clk(nGW));  // open: clr
  assign IO = decoder_2_out0 ? register_1_q : 4'bz;  // Controlled_Buffer controlled_buffer_1
  assign IO = decoder_2_out1 ? register_2_q : 4'bz;  // Controlled_Buffer controlled_buffer_2
  assign IO = decoder_2_out2 ? register_3_q : 4'bz;  // Controlled_Buffer controlled_buffer_3
  assign IO = decoder_2_out3 ? register_4_q : 4'bz;  // Controlled_Buffer controlled_buffer_4

  assign IO_2 = IO;
endmodule

module SN74LS156 (
  input  n1G,
  input  _1C,
  input  [1:0] SEL,
  input  n2G,
  input  _2C,
  output _1Y0,
  output _1Y1,
  output _1Y2,
  output _1Y3,
  output _2Y0,
  output _2Y1,
  output _2Y2,
  output _2Y3
);

  wire and_1_out, and_2_out, decoder_1_out0, decoder_1_out1, decoder_1_out2, decoder_1_out3, decoder_2_out0,
       decoder_2_out1, decoder_2_out2, decoder_2_out3;

  and and_1 (and_1_out, ~n1G, _1C);  // AND_Gate
  and and_2 (and_2_out, ~n2G, _2C);  // AND_Gate
  Decoder #(.select(2), .disabled(0), .enable("false")) decoder_1 (
    .out0(decoder_1_out0), .out1(decoder_1_out1), .out2(decoder_1_out2), .out3(decoder_1_out3), .sel(SEL));
  Decoder #(.select(2), .disabled(0), .enable("false")) decoder_2 (
    .out0(decoder_2_out0), .out1(decoder_2_out1), .out2(decoder_2_out2), .out3(decoder_2_out3), .sel(SEL));
  Pull_Resistor #(.pull(1)) pull_resistor_1 (.node(_1Y2));
  Pull_Resistor #(.pull(1)) pull_resistor_2 (.node(_1Y0));
  Pull_Resistor #(.pull(1)) pull_resistor_3 (.node(_1Y1));
  assign _1Y0 = and_1_out ? ~decoder_1_out0 : 1'bz;  // Controlled_Inverter controlled_inverter_1
  assign _1Y1 = and_1_out ? ~decoder_1_out1 : 1'bz;  // Controlled_Inverter controlled_inverter_2
  assign _1Y2 = and_1_out ? ~decoder_1_out2 : 1'bz;  // Controlled_Inverter controlled_inverter_3
  Pull_Resistor #(.pull(1)) pull_resistor_4 (.node(_2Y2));
  Pull_Resistor #(.pull(1)) pull_resistor_5 (.node(_2Y0));
  Pull_Resistor #(.pull(1)) pull_resistor_6 (.node(_2Y1));
  assign _2Y0 = and_2_out ? ~decoder_2_out0 : 1'bz;  // Controlled_Inverter controlled_inverter_4
  assign _2Y1 = and_2_out ? ~decoder_2_out1 : 1'bz;  // Controlled_Inverter controlled_inverter_5
  assign _2Y2 = and_2_out ? ~decoder_2_out2 : 1'bz;  // Controlled_Inverter controlled_inverter_6
  Pull_Resistor #(.pull(1)) pull_resistor_7 (.node(_1Y3));
  assign _1Y3 = and_1_out ? ~decoder_1_out3 : 1'bz;  // Controlled_Inverter controlled_inverter_7
  Pull_Resistor #(.pull(1)) pull_resistor_8 (.node(_2Y3));
  assign _2Y3 = and_2_out ? ~decoder_2_out3 : 1'bz;  // Controlled_Inverter controlled_inverter_8
endmodule

module _74HCT377 (
  input  [7:0] D,
  input  nEN,
  input  CLK,
  output [7:0] Q
);

  wire not_1_out;

  not not_1 (not_1_out, nEN);
  Register #(.Select("low")) register_1 (.D(D), .en(not_1_out), .Q(Q), .clk(CLK));  // open: clr
endmodule

module _74HCT299 (
  input  [7:0] IO,
  input  S0,
  input  S1,
  input  CP,
  input  nMR,
  input  nOE1,
  input  nOE2,
  output [7:0] IO_2
);

  wire and_1_out, nor_1_out, not_1_out;
  wire [7:0] register_1_q;

  Pull_Resistor #(.pull(1)) pull_resistor_1 (.node(S0));
  Pull_Resistor #(.pull(1)) pull_resistor_2 (.node(S1));
  Pull_Resistor #(.pull(1)) pull_resistor_3 (.node(CP));
  Pull_Resistor #(.pull(1)) pull_resistor_4 (.node(nMR));
  Pull_Resistor #(.pull(1)) pull_resistor_5 (.node(nOE1));
  Pull_Resistor #(.pull(1)) pull_resistor_6 (.node(nOE2));
  and and_1 (and_1_out, S0, S1);
  not not_1 (not_1_out, nMR);
  nor nor_1 (nor_1_out, nOE1, and_1_out, nOE2);
  Register #(.Select("low")) register_1 (.D(IO), .en(and_1_out), .Q(register_1_q), .clk(CP), .clr(not_1_out));
  assign IO_2 = nor_1_out ? register_1_q : 8'bz;  // Controlled_Buffer controlled_buffer_1
endmodule

module _74LS593 (
  input  nCLOAD,
  input  G,
  input  nG,
  input  [7:0] IO,
  input  CCKEN,
  input  nRCO,
  input  nCCKEN,
  input  CCK,
  input  nCCLR,
  input  nRCKEN,
  input  RCK,
  output [7:0] IO_2
);

  wire and_1_out, and_2_out, comparator_1_eq, not_1_out, not_2_out, not_3_out, or_1_out, or_2_out, or_3_out;
  wire [7:0] adder_1_out, multiplexer_1_out, register_1_q, register_2_q;

  Pull_Resistor #(.pull(1)) pull_resistor_1 (.node(nCLOAD));
  Pull_Resistor #(.pull(1)) pull_resistor_2 (.node(G));
  Pull_Resistor #(.pull(1)) pull_resistor_3 (.node(nG));
  Pull_Resistor #(.pull(1)) pull_resistor_4 (.node(CCKEN));
  Pull_Resistor #(.pull(1)) pull_resistor_5 (.node(nCCKEN));
  Pull_Resistor #(.pull(1)) pull_resistor_6 (.node(CCK));
  Pull_Resistor #(.pull(1)) pull_resistor_7 (.node(nCCLR));
  Pull_Resistor #(.pull(1)) pull_resistor_8 (.node(nRCKEN));
  Pull_Resistor #(.pull(1)) pull_resistor_9 (.node(RCK));
  not not_1 (not_1_out, nCLOAD);
  or or_1 (or_1_out, G, ~nG);  // OR_Gate
  Pull_Resistor #(.pull(1)) pull_resistor_10 (.node(IO));
  and and_1 (and_1_out, nCLOAD, or_2_out);
  or or_2 (or_2_out, CCKEN, ~nCCKEN);  // OR_Gate
  not not_2 (not_2_out, nCCLR);
  not not_3 (not_3_out, nRCKEN);
  Register #(.Select("low")) register_1 (.D(IO), .en(not_3_out), .Q(register_1_q), .clk(RCK));  // open: clr
  Adder adder_1 (.a(register_2_q), .b(8'h1), .out(adder_1_out));  // open: cin, cout
  Multiplexer #(.width(8), .enable("false")) multiplexer_1 (
    .in0(register_1_q), .in1(adder_1_out), .out(multiplexer_1_out), .sel(and_1_out));
  Register #(.Select("low")) register_2 (
    .D(multiplexer_1_out), .Q(register_2_q), .clk(or_3_out), .clr(not_2_out));  // open: en
  or or_3 (or_3_out, not_1_out, and_2_out);
  and and_2 (and_2_out, and_1_out, CCK);
  assign IO_2 = or_1_out ? register_2_q : 8'bz;  // Controlled_Buffer controlled_buffer_1
  Comparator comparator_1 (.a(register_2_q), .b({8{1'b1}}), .eq(comparator_1_eq));  // open: gt, lt
  not not_4 (nRCO, comparator_1_eq);

  // Notes on the sheet:
  //   nG: pull=up
  //   CCKEN: pull=up
  //   G: pull=up
  //   nCLOAD: pull=up
  //   IO_2: pull=up
  //   nCCKEN: pull=up
  //   nCCLR: pull=up
  //   CCK: pull=up
  //   nRCKEN: pull=up
  //   RCK: pull=up
endmodule

module _74HCT374 (
  input  [7:0] D,
  input  CP,
  input  nOE,
  output [7:0] Q
);

  wire not_1_out;
  wire [7:0] register_1_q;

  not not_1 (not_1_out, nOE);
  Register #(.Select("low")) register_1 (.D(D), .Q(register_1_q), .clk(CP));  // open: en, clr
  assign Q = not_1_out ? register_1_q : 8'bz;  // Controlled_Buffer controlled_buffer_1
endmodule
