// Digital circuit lcd.dig as structural Verilog
module lcd (
  input  OE,
  input  [7:0] D,
  input  CP,
  input  CLK
);

  wire _7408_1_pin3, _7408_1_pin9, _7408_1_pin10, _7408_1_pin12, _7408_1_pin13, _7414_1_pin2, _7414_1_pin3,
       _7414_1_pin4, _7414_1_pin6, _7414_1_pin9, _7414_1_pin11, _7414_1_pin13, bussplitter_1_d0,
       bussplitter_1_d1, bussplitter_1_d2, bussplitter_1_d3, bussplitter_1_d7, hd44780u_1_busy,
       hd44780u_1_cmdreadstate, not_1_out;
  wire [1:0] hd44780u_1_bitmode;
  wire [2:0] bussplitter_1_d4, hd44780u_1_state;
  wire [3:0] bussplitter_2_d0;
  wire [6:0] hd44780u_1_ac;
  wire [7:0] bussplitter_2_d, hd44780u_1_cmd;

  BusSplitter #(.Bits(8)) bussplitter_1 (
    .D(D), .OE(OE), .D0(bussplitter_1_d0), .D1(bussplitter_1_d1), .D2(bussplitter_1_d2),
    .D3(bussplitter_1_d3), .D4(bussplitter_1_d4[0]), .D5(bussplitter_1_d4[1]), .D6(bussplitter_1_d4[2]),
    .D7(bussplitter_1_d7));
  BusSplitter #(.Bits(8)) bussplitter_2 (
    .D(bussplitter_2_d), .OE(_7414_1_pin6), .D0(bussplitter_2_d0[0]), .D1(bussplitter_2_d0[1]),
    .D2(bussplitter_2_d0[2]), .D3(bussplitter_2_d0[3]), .D4(bussplitter_1_d0), .D5(bussplitter_1_d1),
    .D6(bussplitter_1_d2), .D7(bussplitter_1_d3));
  // NotConnected on bussplitter_2_d0
  // NotConnected on bussplitter_1_d4
  _7414 _7414_1 (
    .pin1(CP), .pin2(_7414_1_pin2), .pin3(_7414_1_pin3), .pin4(_7414_1_pin4), .pin5(OE), .pin6(_7414_1_pin6),
    .pin7(1'b0), .pin9(_7414_1_pin9), .pin11(_7414_1_pin11), .pin13(_7414_1_pin13), .pin14(1'b1));  // open: pin8, pin10, pin12
  _7408 _7408_1 (
    .pin1(OE), .pin2(bussplitter_1_d7), .pin3(_7408_1_pin3), .pin4(_7414_1_pin2), .pin5(OE),
    .pin6(_7414_1_pin3), .pin7(1'b0), .pin9(_7408_1_pin9), .pin10(_7408_1_pin10), .pin12(_7408_1_pin12),
    .pin13(_7408_1_pin13), .pin14(1'b1));  // open: pin8, pin11
  // NotConnected on _7414_1_pin13
  // NotConnected on _7414_1_pin11
  // NotConnected on _7414_1_pin9
  // NotConnected on _7408_1_pin13
  // NotConnected on _7408_1_pin12
  // NotConnected on _7408_1_pin10
  // NotConnected on _7408_1_pin9
  HD44780U hd44780u_1 (
    .DB(bussplitter_2_d), .E(_7414_1_pin4), .RW(_7414_1_pin6), .RS(_7408_1_pin3), .CLK(CLK),
    .AC(hd44780u_1_ac), .State(hd44780u_1_state), .Busy(hd44780u_1_busy),
    .CmdReadState(hd44780u_1_cmdreadstate), .BitMode(hd44780u_1_bitmode), .Cmd(hd44780u_1_cmd));
  // Probe on hd44780u_1_ac
  // Probe on hd44780u_1_state
  // Probe on hd44780u_1_busy
  // Probe on hd44780u_1_bitmode
  // Probe on hd44780u_1_cmd
  not not_1 (not_1_out, hd44780u_1_busy);
  // Probe on hd44780u_1_cmdreadstate
  Break #(.Cycles(1000000000)) break_1 (.brk(hd44780u_1_cmdreadstate));
  Break #(.Cycles(1000000000)) break_2 (.brk(not_1_out));
endmodule

/* Test case:
OE_ CP D_out
1   X  Z
*/
