// Digital circuit spicomp.dig as structural Verilog
module spicomp (
  input  RST,
  input  CLK
);

  wire and_1_out, bitselector_1_out, comparator_1_eq, not_1_out, serial_rom_1_so;
  wire [2:0] counter_1_out;
  wire [5:3] counter_1_out_2;
  wire [7:0] IR_q, multiplexer_1_out, PC0_q, PC1_q, PC2_q, PROG_q, register_1_q;
  wire [19:0] serial_rom_1_rom_addr;

  Counter #(.Bits(6)) counter_1 (.en(1'b1), .C(CLK), .clr(RST), .out({counter_1_out_2, counter_1_out}));  // open: ovf
  // Probe bit on counter_1_out
  // Probe byte on counter_1_out_2
  shift_reg PC2 (.SCLK(1'b0), .SIN(1'b1), .EN(1'b1), .RST(RST), .Q(PC2_q));  // open: OF
  shift_reg PC1 (.SCLK(1'b0), .SIN(1'b1), .EN(1'b1), .RST(RST), .Q(PC1_q));  // open: OF
  shift_reg PC0 (.SCLK(1'b0), .SIN(1'b1), .EN(1'b1), .RST(RST), .Q(PC0_q));  // open: OF
  Multiplexer #(.Selector_Bits(3), .Bits(8)) multiplexer_1 (
    .sel(counter_1_out_2), .in_0(8'h3), .in_1(PC2_q), .in_2(PC1_q), .in_3(PC0_q), .in_4({8{1'b1}}),
    .in_5({8{1'b1}}), .in_6({8{1'b1}}), .in_7({8{1'b1}}), .out(multiplexer_1_out));
  BitSelector #(.Selector_Bits(3)) bitselector_1 (.in(multiplexer_1_out), .sel(counter_1_out), .out(bitselector_1_out));
  Comparator #(.Bits(3)) comparator_1 (.a(3'b000), .b(counter_1_out), .eq(comparator_1_eq));  // open: gt, lt
  not not_1 (not_1_out, CLK);
  serial_rom serial_rom_1 (
    .SCLK(CLK), .SI(bitselector_1_out), .CE(RST), .HOLD(1'b1), .ROM_D(PROG_q), .SO(serial_rom_1_so),
    .ROM_ADDR(serial_rom_1_rom_addr));  // open: TEST, bit, byte
  RAMAsync #(.AddrBits(20), .Bits(8)) PROG (.A(serial_rom_1_rom_addr), .D({8{1'b0}}), .we(1'b0), .Q(PROG_q));
  and and_1 (and_1_out, comparator_1_eq, not_1_out);
  // Probe ROM_DATA on PROG_q
  // Probe ROM_ADDR on serial_rom_1_rom_addr
  shift_reg IR (.SCLK(CLK), .SIN(serial_rom_1_so), .EN(counter_1_out_2[5]), .RST(RST), .Q(IR_q));  // open: OF
  Register #(.Bits(8)) register_1 (.D(IR_q), .C(and_1_out), .en(counter_1_out_2[5]), .Q(register_1_q));
  // Probe IR_SR on IR_q
  // Probe IR on register_1_q

  // Notes on the sheet:
  //   RST: default 1
endmodule

/* Test case boot:
           RST  CLK IR
	   0    0   0
loop(n,32)
           0    0   X
           0    1   X
end loop
loop(n,8)
           0    0   X
           0    1   X
end loop
           0    0   0xAB
loop(n,7)
           0    C   0xAB
end loop
           0    0   0xAB
           0    1   0xAB
           0    0   0xCD
memory PROG(0x0)=0xAB;
memory PROG(0x1)=0xCD;
*/
